// Logisim project assignment1.circ as structural Verilog: 2 circuits, main circuit main
module main (
);

  wire demultiplexer_1_out0, demultiplexer_1_out1, demultiplexer_1_out2, demultiplexer_1_out3,
       demultiplexer_1_out4, demultiplexer_1_out5, demultiplexer_1_out6, demultiplexer_1_out7,
       demultiplexer_1_out8;
  wire [1:0] joystick_1_x, joystick_1_y;
  wire [3:0] logic_1_z;

  // Probe on joystick_1_x
  Joystick #(.bits(2)) joystick_1 (.x(joystick_1_x), .y(joystick_1_y));
  // Probe on joystick_1_y
  \logic  logic_1 (.x(joystick_1_x), .y(joystick_1_y), .z(logic_1_z));
  Demultiplexer #(.select(4)) demultiplexer_1 (
    .out0(demultiplexer_1_out0), .out1(demultiplexer_1_out1), .out2(demultiplexer_1_out2),
    .out3(demultiplexer_1_out3), .out4(demultiplexer_1_out4), .out5(demultiplexer_1_out5),
    .out6(demultiplexer_1_out6), .out7(demultiplexer_1_out7), .out8(demultiplexer_1_out8), .in(1'b1),
    .sel(logic_1_z));  // open: out9, out10, out11, out12, out13, out14, out15, en
  // Probe on logic_1_z
  LED _4 (.in(demultiplexer_1_out4));
  LED _3 (.in(demultiplexer_1_out3));
  LED center (.in(demultiplexer_1_out0));
  LED _5 (.in(demultiplexer_1_out5));
  LED _1 (.in(demultiplexer_1_out1));
  LED _2 (.in(demultiplexer_1_out2));
  LED _8 (.in(demultiplexer_1_out8));
  LED _6 (.in(demultiplexer_1_out6));
  LED _7 (.in(demultiplexer_1_out7));

  // Notes on the sheet:
  //   Your circuit here
endmodule

module \logic  (
  input  [1:0] x,
  input  [1:0] y,
  output [3:0] z
);

  wire and_1_out, and_2_out, and_3_out, and_4_out, and_6_out, and_7_out, and_8_out, and_9_out, and_10_out,
       and_11_out, not_1_out, not_2_out, not_3_out, not_4_out, or_1_out;

  not not_1 (not_1_out, x[0]);
  not not_2 (not_2_out, x[1]);
  and and_1 (and_1_out, y[0], not_4_out);
  not not_3 (not_3_out, y[0]);
  not not_4 (not_4_out, y[1]);
  and and_2 (and_2_out, not_1_out, x[1]);
  and and_3 (and_3_out, and_6_out, and_1_out);
  and and_4 (and_4_out, and_2_out, y[0]);
  and and_5 (z[0], x[0], y[0]);
  or or_1 (or_1_out, and_4_out, and_3_out);
  and and_6 (and_6_out, not_2_out, x[0]);
  and and_7 (and_7_out, y[0], y[1]);
  and and_8 (and_8_out, x[0], x[1]);
  and and_9 (and_9_out, and_6_out, y[1]);
  and and_10 (and_10_out, x[1], and_7_out);
  or or_2 (z[2], and_9_out, and_10_out);
  and and_11 (and_11_out, not_3_out, y[1]);
  and and_12 (z[3], and_8_out, and_11_out);
  or or_3 (z[1], and_10_out, or_1_out);
endmodule
