// Logisim project assignment2practice.circ as structural Verilog: 3 circuits, main circuit main
module main (
);

  wire clear, comparator_2_eq, comparator_3_eq, comparator_4_eq, L0, L1, L2, latch1, match, open, reset, zero;
  wire [1:0] joystick_1_x, joystick_1_y;
  wire [3:0] logic1_1_f, register_1_q, register_2_q, register_3_q;
  wire [5:3] rom_1_data, y0_q;

  Button Reset_Lock (.out(reset));
  logic1 logic1_1 (.x(joystick_1_x), .y(joystick_1_y), .f(logic1_1_f));
  Joystick #(.bits(2)) joystick_1 (.x(joystick_1_x), .y(joystick_1_y));
  // Probe on logic1_1_f
  Comparator #(.width(4), .mode("unsigned")) comparator_1 (.a(logic1_1_f), .b(4'b0000), .eq(zero));  // open: gt, lt
  LED Green_open (.in(open));
  Register #(.width(4)) register_1 (.D(logic1_1_f), .en(L0), .Q(register_1_q), .clk(latch1), .clr(clear));
  Comparator #(.width(4)) comparator_2 (.a(4'b0001), .b(register_1_q), .eq(comparator_2_eq));  // open: gt, lt
  Register #(.width(4)) register_2 (.D(logic1_1_f), .en(L1), .Q(register_2_q), .clk(latch1), .clr(clear));
  // Probe on {y0_q, match, zero, reset}
  Comparator #(.width(4)) comparator_3 (.a(4'b0010), .b(register_2_q), .eq(comparator_3_eq));  // open: gt, lt
  Register #(.width(4)) register_3 (.D(logic1_1_f), .en(L2), .Q(register_3_q), .clk(latch1), .clr(clear));
  Clock clock_1 (.out(latch1));
  Comparator #(.width(4)) comparator_4 (.a(4'b0011), .b(register_3_q), .eq(comparator_4_eq));  // open: gt, lt
  and u_match (match, comparator_4_eq, comparator_3_eq, comparator_2_eq);
  ROM #(.addrWidth(6)) rom_1 (
    .addr({y0_q, match, zero, reset}), .data({open, clear, rom_1_data, L2, L1, L0}));  // open: sel
  D_Flip_Flop y2 (.clk(latch1), .D(rom_1_data[5]), .Q(y0_q[5]), .reset(clear));  // open: Qn, preset, en
  D_Flip_Flop y1 (.clk(latch1), .D(rom_1_data[4]), .Q(y0_q[4]), .reset(clear));  // open: Qn, preset, en
  D_Flip_Flop y0 (.clk(latch1), .D(rom_1_data[3]), .Q(y0_q[3]), .reset(clear));  // open: Qn, preset, en
  // Probe on {open, clear, rom_1_data, L2, L1, L0}

  // Other names for the same wires on the sheet: latch2 = latch1; latch3 = latch1

  // Notes on the sheet:
  //   operate the lock here
  //   is the lock open or closed?
  //   set combination here
  //   contents of rom_1 (hex, n*v repeats v):
  //   9 40 0 40 4*0 8 8 10 40 4*8 1a 10 10 40 4*10 18 18 20 40 4*18 2c 20 20 40 4*20 28 28 30 40 b8 28 b8
  //   28 30 30 38 40 4*30 38 38 38 40 b8 38 b8 40
endmodule

// l0
module logic0 (
  input  [1:0] x,
  input  [1:0] y,
  output [3:0] f
);

  wire nand_1_out, nand_2_out, nand_3_out, nand_4_out, nand_5_out, nand_6_out, nand_7_out, nand_8_out,
       nand_9_out, not_1_out, not_2_out, not_3_out, not_4_out;

  // Probe on x
  // Probe on y
  not not_1 (not_1_out, x[1]);
  not not_2 (not_2_out, x[0]);
  not not_3 (not_3_out, y[1]);
  not not_4 (not_4_out, y[0]);
  nand nand_1 (nand_1_out, x[0], not_3_out);
  nand nand_2 (nand_2_out, not_2_out, y[1], y[0]);
  nand nand_3 (nand_3_out, x[1], x[0], not_4_out);
  nand nand_4 (nand_4_out, x[1], not_3_out);
  nand nand_5 (nand_5_out, not_2_out, y[0]);
  nand nand_6 (nand_6_out, not_1_out, y[1], y[0]);
  nand nand_7 (nand_7_out, not_1_out, y[1]);
  nand nand_8 (nand_8_out, x[0], y[1], not_4_out);
  nand nand_9 (nand_9_out, not_2_out, y[1], y[0]);
  and and_1 (f[3], x[1], x[0], y[1], y[0]);
  nand nand_10 (f[0], nand_1_out, nand_2_out, nand_3_out);
  nand nand_11 (f[1], nand_4_out, nand_5_out, nand_6_out);
  nand nand_12 (f[2], nand_7_out, nand_8_out, nand_9_out);
endmodule

// l1
module logic1 (
  input  [1:0] x,
  input  [1:0] y,
  output [3:0] f
);

  wire nand_1_out, nand_2_out, nand_3_out, nand_4_out, nand_5_out, not_1_out, not_2_out, not_3_out, not_4_out;

  // Probe on x
  // Probe on y
  not not_1 (not_1_out, x[1]);
  not not_2 (not_2_out, x[0]);
  not not_3 (not_3_out, y[1]);
  not not_4 (not_4_out, y[0]);
  nand nand_1 (nand_1_out, not_1_out, not_3_out);
  nand nand_2 (nand_2_out, x[1], y[1], y[0]);
  nand nand_3 (nand_3_out, not_2_out, y[0]);
  nand nand_4 (nand_4_out, y[1], y[0]);
  nand nand_5 (nand_5_out, not_1_out, y[1]);
  and and_1 (f[0], x[0], y[0]);
  nand nand_6 (f[1], nand_1_out, nand_2_out, nand_3_out);
  nand nand_7 (f[2], nand_4_out, nand_5_out);
  and and_2 (f[3], x[1], x[0], not_4_out);
endmodule
